// Logisim project circuito de soma.circ as structural Verilog
module Add_1 (
  input  A,
  input  B,
  input  Vem_1,
  output S,
  output Vai_1
);

  wire and_1_out, and_2_out, or_1_out, xor_1_out;

  xor xor_1 (xor_1_out, A, B);
  or or_1 (or_1_out, B, Vem_1);
  xor xor_2 (S, xor_1_out, Vem_1);
  and and_1 (and_1_out, or_1_out, A);
  and and_2 (and_2_out, B, Vem_1);
  or or_2 (Vai_1, and_1_out, and_2_out);
endmodule

module Add_4 (
);

  Add_1 add_1_1 ();  // open: S, Vai_1, A, B, Vem_1
  Add_1 add_1_2 ();  // open: S, Vai_1, A, B, Vem_1
  Add_1 add_1_3 ();  // open: S, Vai_1, A, B, Vem_1
  Add_1 add_1_4 ();  // open: S, Vai_1, A, B, Vem_1
endmodule
